# Fritzing sketch Circuito-testes-sensores-ambientais (saved by Fritzing 0.9.2b)

parts:
  Part1 = Arduino Uno (Rev3)
  C1 = Tantalum Capacitor [capacitance="1 μF" package="C 6032 [SMD, tantalum]"]
  C2 = Tantalum Capacitor [capacitance="1 μF" package="C 6032 [SMD, tantalum]"]
  U1 = V_REG_LD1085 [package=d2pack_a]
  Part2 = Ambient Light Sensor (TEMT6000 Breakout Board)
  R1 = Temperature Sensor (Thermistor) [thermistor_type=NTC package=THT]
  R2 = Resistor [tolerance=±5% resistance=10k package="2512 [SMD]"]
  R3 = Photocell (LDR) [package=THT]
  R4 = Resistor [tolerance=±5% resistance=10k package="2512 [SMD]"]
  RHT1 = Humidity and Temperature Sensor RHT03
  Part3 = Digital Temperature Sensor Breakout - TMP102
  Part4 = Barometric Pressure Sensor - BMP085 Breakout
  R5 = Resistor [tolerance=±5% resistance=3.3k package="2512 [SMD]"]

nets:
  N1: Part1.A0, Part2.S
  N2: Part1.A1, R1.pin_0, R2.Pin_0
  N3: Part1.A2, R3.pin_0, R4.Pin_0
  N4: Part1.A4/SDA, Part3.SDA, Part4.SDA
  N5: Part1.A5/SCL, Part3.SCL, Part4.SCL
  N6: Part1.D2, RHT1.Data-signal, R5.Pin_1
  VCC: Part1.5V, C2.+, U1.IN, Part2.VCC, R1.pin_1, R3.pin_1, RHT1.Vcc, R5.Pin_0
  GND: Part1.GND, C1.-, C2.-, U1.ADJ, Part2.GND, R2.Pin_1, R4.Pin_1, RHT1.GND_2, Part3.GND, Part4.EOC
  N7: C1.+, U1.OUT, Part3.V+, Part4.GND

notes:
  5V
  3.3V
  GND
  22uF
  AMS1117
  Reg. 3.3V
  AM2302
  DHT22
  NTC
  LDR
  TEMT6000
  Si7021
  SHT21
  BMP280
  SCL
  SDA
  3k3
  10k
